# Fritzing sketch RP2040 DCC Encoder (saved by Fritzing 1.0.3b)
perfboards: 1

parts:
  R1 = Resistor [tolerance=±5% power=0.25W resistance=1k package=THT]
  R2 = Resistor [tolerance=±5% power=0.25W resistance=1k package=THT]
  R3 = Resistor [tolerance=±5% power=0.25W resistance=1k package=THT]
  D1 = Rectifier Diode [part_number=1N4001 package="300 mil [THT]"]
  D2 = Rectifier Diode [part_number=1N4001 package="300 mil [THT]"]
  D3 = Rectifier Diode [part_number=1N4001 package="300 mil [THT]"]
  D4 = Rectifier Diode [part_number=1N4001 package="300 mil [THT]"]
  U1 = Voltage Regulator - 5V [package="TO220 [THT]"]
  J1 = female pin header, 2 pins [form="♀ (female)"]
  Waveshare1 = Waveshare rp2040-zero tht [package=THT]
  LED1 = RGB LED (com. cathode, rgb) [color="Red (633nm)" current=0.030A package="5 mm [THT]"]  # not connected
  R4 = Resistor [tolerance=±5% power=0.25W resistance=330 package=THT]
  R5 = Resistor [tolerance=±5% power=0.25W resistance=220 package=THT]
  R6 = Resistor [tolerance=±5% power=0.25W resistance=220 package=THT]
  J2 = female pin header, 4 pins [form="♀ (female)"]
  Q1 = NPN-Transistor [package="TO92 [THT]"]
  C1 = Electrolytic Capacitor [capacitance=0.22µF voltage=16V package="100 mil [THT, electrolytic]"]

nets:
  N1: R1.Pin_0, R2.Pin_0, Q1.B
  N2: R1.Pin_1, D2.cathode, D4.anode, J1.pin2
  N3: R2.Pin_1, D2.anode, D3.anode, U1.GND, Waveshare1.Pin_2, J2.pin2, C1.-
  N4: R3.Pin_0, Waveshare1.Pin_3
  N5: R3.Pin_1, Q1.C
  N6: D1.cathode, D4.cathode, U1.input_voltage, C1.+
  N7: D1.anode, D3.cathode, J1.pin1
  N8: U1.output_voltage, Waveshare1.Pin_1
  N9: Waveshare1.Pin_9, Q1.E
  N10: Waveshare1.Pin_21, R4.Pin_0
  N11: Waveshare1.Pin_22, R5.Pin_0
  N12: Waveshare1.Pin_23, R6.Pin_0
  N13: R4.Pin_1, J2.pin1
  N14: R5.Pin_1, J2.pin3
  N15: R6.Pin_1, J2.pin4

notes:
  Rail Connection
  RGB LED
  Connector -->
  DCC Rail
  RGB LED Connection

custom parts:
  Waveshare rp2040-zero tht: .RP2040-Zero, A Low-Cost, High-Performance Pico-Like MCU Board Based On Raspberry Pi Microcontroller RP2040. This varant is THT without the extra connections.
